# Fritzing sketch rgb_led (saved by Fritzing 0.6.5b)
breadboards: 1

parts:
  RGB_LED_(common_cathode) = RGB LED (com. cathode, rbg) [package="5 mm [THT]"]
  R1 = Resistor [tolerance=±5% resistance=220 package=THT]
  R2 = Resistor [tolerance=±5% resistance=220 package=THT]
  R3 = Resistor [tolerance=±5% resistance=220 package=THT]
  Arduino1 = Arduino

nets:
  N1: RGB_LED_(common_cathode).red_anode, R1.Pin_1
  N2: RGB_LED_(common_cathode).common_cathode, Arduino1.3V3
  N3: RGB_LED_(common_cathode).blue_anode, R2.Pin_1
  N4: RGB_LED_(common_cathode).green_anode, R3.Pin_1
  N5: R1.Pin_0, Arduino1.D6
  N6: R2.Pin_0, Arduino1.D5
  N7: R3.Pin_0, Arduino1.D3
